# Fritzing sketch esp8266_lamp (saved by Fritzing 0.9.3b)

parts:
  U1 = ESP8266 ESP-01 Upgraded WiFi Module [part_number=ESP8266]
  S1 = Pushbutton [package="[THT]"]
  M1 = RioRand LM2596
  LED1 = LED - 5mm [color="Red (633nm)" current=0.030 package="5 mm [THT]"]
  X1 = USB Connectors [package=usb-microb]
  Q2 = PNP-Transistor [package="TO92 [THT]"]

nets:
  N1: U1.RXD, S1.Pin_1, S1.Pin_2
  N2: U1.VCC, M1.Pin_3
  N3: U1.GPIO_2, Q2.B
  N4: U1.GND, M1.Pin_4, Q2.C
  N5: M1.Pin_1, X1.VBUS
  N6: M1.Pin_2, X1.GND
  N7: LED1.anode, Q2.E

custom parts:
  ESP8266 ESP-01 Upgraded WiFi Module: Upgraded Version ESP-01,all Flash are upgraded to 1M byte.Also support Cloud service remote transmission.
